# Fritzing sketch Semaforo (saved by Fritzing 0.8.3b)
breadboards: 1

parts:
  Componente1 = Arduino Uno (Rev3)
  S1 = Pushbutton [package="[THT]"]
  R1 = Resistor [tolerance=±5% resistance=10k package=THT]
  LED1 = LED - 5mm [color="Green (555nm)" package="5 mm [THT]"]
  LED2 = LED - 5mm [color="Yellow (585nm)" package="5 mm [THT]"]
  LED3 = LED - 5mm [color="Red (633nm)" package="5 mm [THT]"]
  R2 = Resistor [tolerance=±5% resistance=220 package=THT]
  R3 = Resistor [tolerance=±5% resistance=220 package=THT]
  R4 = Resistor [tolerance=±5% resistance=220 package=THT]
  J1 = Piezo Speaker

nets:
  N1: Componente1.ICSP_SCK, Componente1.D13/SCK, J1.pin2
  N2: Componente1.GND, R1.Pin_1, R2.Pin_1, R3.Pin_1, R4.Pin_1, J1.pin1
  N3: Componente1.D2, S1.Pin_1, S1.Pin_2, R1.Pin_0
  N4: Componente1.D3_PWM, LED1.anode
  N5: Componente1.D4, LED2.anode
  N6: Componente1.D5_PWM, LED3.anode
  N7: Componente1.5V, S1.Pin_3, S1.Pin_4
  N8: LED1.cathode, R2.Pin_0
  N9: LED2.cathode, R3.Pin_0
  N10: LED3.cathode, R4.Pin_0
